# Fritzing sketch fire_detection_robot (saved by Fritzing 1.0.5)
breadboards: 2

parts:
  HC-SR04_Sensor_Left = HC-SR04 Ultrasonic Distance Sensor
  MQ-2 = MQ-2 Gas Sensor
  L298N = L298_BRIDGE_DRIVER [package=powerso20]
  DC_Motor_Left = gear-motor
  DC_Motor_Right = gear-motor
  GY-NEO6MV3 = SUP500F [package=sup500f]
  SX1278 = Osoyoo SX1278-ra-02
  ANT1 = Antenna  # not connected
  DC-DC_Converter_5V = RioRand LM2596
  DC-DC_Converter_6V = RioRand LM2596
  Steering_Servo = Basic Servo
  Εξάρτημα2 = INA 260
  microSD1 = MicroSD Card Module
  HC-SR04_Sensor_Front = HC-SR04 Ultrasonic Distance Sensor
  HC-SR04_Sensor_Right = HC-SR04 Ultrasonic Distance Sensor
  Εξάρτημα3 = Arduino Mega ADK (Rev3)
  U1 = LIPO-2000mAh [package=lipo-2000]
  DC-DC_Converter_6V1 = RioRand LM2596

nets:
  VCC: HC-SR04_Sensor_Left.VCC, MQ-2.VCC, GY-NEO6MV3.VCC, DC-DC_Converter_5V.Pin_3, Steering_Servo.vcc, microSD1.VCC, HC-SR04_Sensor_Front.VCC, HC-SR04_Sensor_Right.VCC, Εξάρτημα3.VIN
  N1: HC-SR04_Sensor_Left.TRIG, Εξάρτημα3.D30
  N2: HC-SR04_Sensor_Left.ECHO, Εξάρτημα3.D31
  GND: HC-SR04_Sensor_Left.GND, MQ-2.GND, GY-NEO6MV3.GND, SX1278.GND, Steering_Servo.gnd, microSD1.GND, HC-SR04_Sensor_Front.GND, HC-SR04_Sensor_Right.GND, Εξάρτημα3.GND
  N3: MQ-2.AO, Εξάρτημα3.A0
  N4: L298N.GND, DC-DC_Converter_6V.Pin_4, DC-DC_Converter_6V1.Pin_4
  N5: L298N.OUT1, DC_Motor_Left.pin_2
  N6: L298N.OUT2, DC_Motor_Left.pin_1
  N7: L298N.VS, DC-DC_Converter_6V.Pin_3
  N8: L298N.IN1, Εξάρτημα3.D22
  N9: L298N.ENA, Εξάρτημα3.D9_PWM
  N10: L298N.IN2, Εξάρτημα3.D23
  N11: L298N.VSS, DC-DC_Converter_6V1.Pin_3
  N12: L298N.IN3, Εξάρτημα3.D24
  N13: L298N.ENB, Εξάρτημα3.D10_PWM
  N14: L298N.IN4, Εξάρτημα3.D25
  N15: L298N.OUT3, DC_Motor_Right.pin_1
  N16: L298N.OUT4, DC_Motor_Right.pin_2
  N17: GY-NEO6MV3.RX-I, Εξάρτημα3.D1/TX0
  N18: GY-NEO6MV3.TX-O, Εξάρτημα3.D0/RX0
  N19: GY-NEO6MV3.PPS, Εξάρτημα3.D2_PWM
  3.3V: SX1278.3.3V, Εξάρτημα3.3V3
  N20: SX1278.RST, Εξάρτημα3.D39
  N21: SX1278.DIO0, Εξάρτημα3.D41
  N22: SX1278.SCK, Εξάρτημα3.D43
  N23: SX1278.MISO, Εξάρτημα3.D45
  N24: SX1278.MOSI, Εξάρτημα3.D47
  N25: SX1278.NSS, Εξάρτημα3.D49
  N26: DC-DC_Converter_5V.Pin_1, DC-DC_Converter_6V.Pin_1, Εξάρτημα2.IN-, DC-DC_Converter_6V1.Pin_1
  N27: DC-DC_Converter_5V.Pin_2, DC-DC_Converter_6V.Pin_2, Εξάρτημα2.GND, U1.-, DC-DC_Converter_6V1.Pin_2
  N28: Steering_Servo.pulse, Εξάρτημα3.D11_PWM
  N29: Εξάρτημα2.SCL, Εξάρτημα3.D21/SCL
  N30: Εξάρτημα2.SDA, Εξάρτημα3.D20/SDA
  N31: Εξάρτημα2.IN+, U1.+
  N32: microSD1.MISO, Εξάρτημα3.D50/MISO
  N33: microSD1.MOSI, Εξάρτημα3.D51/MOSI
  N34: microSD1.SCK, Εξάρτημα3.D52/SCK
  N35: microSD1.CS, Εξάρτημα3.D53/SS
  N36: HC-SR04_Sensor_Front.TRIG, Εξάρτημα3.D32
  N37: HC-SR04_Sensor_Front.ECHO, Εξάρτημα3.D33
  N38: HC-SR04_Sensor_Right.TRIG, Εξάρτημα3.D34
  N39: HC-SR04_Sensor_Right.ECHO, Εξάρτημα3.D35

notes:
  GND:Black
  VCC: Red
  RX: Yellow (D1)
  TX: Green (D0)
  PPS: Blue (D2)
  GND:Black
  VCC: Red (+5V)
  Trig: Yellow (34)
  Echo: Green (35)
  GND:Black
  VCC: Red (+5V)
  Trig: Yellow (30)
  Echo: Green (31)
  GND:Black
  VCC: Red (+5V)
  Trig: Yellow (32)
  Echo: Green (33)
  **PG6SD**
  GND:Black
  VCC: Red
  MISO: Purple
  MOSI: Orange
  SCK: Blue
  CS: Yellow (SS)
  **SX1278**
  GND:Black
  VCC: Orange (3.3V)
  MISO: Purple (45)
  MOSI: Orange (47)
  SCK: Blue (43)
  NSS: Yellow (49)
  RST: Grey (39)
  DIO0: Cyan (41)
  **INA260**
  GND:Black
  Vin+: Red
  Vin-: Red
  SCL: Pink (21)
  SDA: Cyan (20)
  **L298**
  1,10: Black (DC-DC Left Out-)
  6: Red (DC-DC Left Out+)
  7,8,9: Orange (22,9,23 - IN1, ENA, IN2)
  11,20: Black (DC-DC Right Out-)
  12: Red (DC-DC Out+)
  13,14,15: Purple (24,10,25 - IN3, ENB, IN4)

custom parts:
  MQ-2 Gas Sensor: MQ-2 Gas Sensor module of ZHIYU Sensor Kit
  Osoyoo SX1278-ra-02: Osoyoo Long Distance wireless transceiver Uart LoRa Module.
  INA 260: Rev. B, add copy
